// Logisim project 学习.circ as structural Verilog: 24 circuits, main circuit test
module main (
  input  in_1
);
endmodule

module \test_上拉电阻  (
  input  in_1,
  output out_2
);

  Pull_Resistor #(.pull(1)) pull_resistor_1 (.node(in_1));

  assign out_2 = in_1;
endmodule

module test (
);

  \应用1_按键转换  \u_应用1_按键转换_1  ();  // open: CLK, clear, _1, _2, _3, _4, _5, _6, _7, _8, _9, _0, OUT, _3_2, _2_2, _1_2, _0_2
endmodule

module \一位加法器  (
  input  A,
  input  B,
  input  CI,
  output S,
  output CO
);

  wire and_1_out, and_2_out, xor_1_out;

  xor xor_1 (xor_1_out, A, B);
  and and_1 (and_1_out, A, B);
  and and_2 (and_2_out, xor_1_out, CI);
  xor xor_2 (S, xor_1_out, CI);
  or or_1 (CO, and_1_out, and_2_out);
endmodule

module \_4位加法器  (
  input  CI,
  input  A0,
  input  B0,
  input  A1,
  input  B1,
  input  A2,
  input  B2,
  input  A3,
  input  B3,
  output S0,
  output S1,
  output S2,
  output S3,
  output CO
);

  wire \一位加法器_1_co , \一位加法器_2_co , \一位加法器_3_co ;

  \一位加法器  \u_一位加法器_1  (.A(A0), .B(B0), .CI(CI), .S(S0), .CO(\一位加法器_1_co ));
  \一位加法器  \u_一位加法器_2  (.A(A1), .B(B1), .CI(\一位加法器_1_co ), .S(S1), .CO(\一位加法器_2_co ));
  \一位加法器  \u_一位加法器_3  (.A(A2), .B(B2), .CI(\一位加法器_2_co ), .S(S2), .CO(\一位加法器_3_co ));
  \一位加法器  \u_一位加法器_4  (.A(A3), .B(B3), .CI(\一位加法器_3_co ), .S(S3), .CO(CO));
endmodule

module \_2位并行加法器  (
  input  CI,
  input  A0,
  input  B0,
  input  A1,
  input  B1,
  output S0,
  output S1,
  output CO
);

  wire and_1_out, and_2_out, and_3_out, and_4_out, and_5_out, and_6_out, or_1_out, or_2_out, xor_1_out,
       xor_2_out;

  and and_1 (and_1_out, A0, B0);
  and and_2 (and_2_out, A1, B1);
  xor xor_1 (xor_1_out, A0, B0);
  and and_3 (and_3_out, xor_1_out, CI);
  xor xor_2 (xor_2_out, A1, B1);
  and and_4 (and_4_out, and_1_out, xor_2_out);
  or or_1 (or_1_out, and_2_out, and_4_out);
  or or_2 (or_2_out, and_1_out, and_3_out);
  and and_5 (and_5_out, xor_1_out, xor_2_out);
  and and_6 (and_6_out, CI, and_5_out);
  or or_3 (CO, or_1_out, and_6_out);
  xor xor_3 (S0, CI, xor_1_out);
  xor xor_4 (S1, or_2_out, xor_2_out);
endmodule

module \_4位并行加法器  (
  input  CI,
  input  A0,
  input  B0,
  input  A1,
  input  B1,
  input  A2,
  input  B2,
  input  A3,
  input  B3,
  output S0,
  output S1,
  output S2,
  output S3,
  output CO
);

  wire CI0P0_out, CI0P0P1_out, CI0P0P1P2_out, CI0P0P1P2P3_out, CO0_out, CO1_out, CO2_out, G0_out, G0P1_out,
       G0P1P2_out, G0P1P2P3_out, G1_out, G1P2_out, G1P2P3_out, G2_out, G2P3_out, G3_out, or_1_out, or_2_out,
       or_3_out, or_4_out, or_5_out, or_6_out, P0_out, P1_out, P2_out, P3_out;

  xor P0 (P0_out, B0, A0);
  and G0 (G0_out, A0, B0);
  xor P1 (P1_out, B1, A1);
  and G1 (G1_out, A1, B1);
  xor P2 (P2_out, B2, A2);
  and G2 (G2_out, A2, B2);
  xor P3 (P3_out, B3, A3);
  and G3 (G3_out, A3, B3);
  and CI0P0 (CI0P0_out, CI, P0_out);
  and G0P1 (G0P1_out, G0_out, P1_out);
  and G1P2 (G1P2_out, G1_out, P2_out);
  and G2P3 (G2P3_out, G2_out, P3_out);
  and CI0P0P1 (CI0P0P1_out, CI0P0_out, P1_out);
  and G0P1P2 (G0P1P2_out, G0P1_out, P2_out);
  and G1P2P3 (G1P2P3_out, G1P2_out, P3_out);
  and CI0P0P1P2 (CI0P0P1P2_out, CI0P0P1_out, P2_out);
  and G0P1P2P3 (G0P1P2P3_out, G0P1P2_out, P3_out);
  and CI0P0P1P2P3 (CI0P0P1P2P3_out, CI0P0P1P2_out, P3_out);
  or CO0 (CO0_out, G0_out, CI0P0_out);
  or or_1 (or_1_out, G1_out, G0P1_out);
  or or_2 (or_2_out, G2_out, G1P2_out);
  or or_3 (or_3_out, G3_out, G2P3_out);
  or CO1 (CO1_out, CI0P0P1_out, or_1_out);
  or or_4 (or_4_out, G0P1P2_out, or_2_out);
  or or_5 (or_5_out, G1P2P3_out, or_3_out);
  or CO2 (CO2_out, CI0P0P1P2_out, or_4_out);
  or or_6 (or_6_out, G0P1P2P3_out, or_5_out);
  or CO3 (CO, CI0P0P1P2P3_out, or_6_out);
  xor u_S0 (S0, CI, P0_out);
  xor u_S1 (S1, CO0_out, P1_out);
  xor u_S2 (S2, CO1_out, P2_out);
  xor u_S3 (S3, CO2_out, P3_out);
endmodule

module \test_4位并行加法器  (
  input  [3:0] in_1,
  input  [3:0] in_2,
  output out_3
);

  wire [3:0] adder_1_out, \n4位并行加法器_1_s0 ;
  wire [4:4] adder_1_cout, \n4位并行加法器_1_co ;

  Adder #(.width(4)) adder_1 (.a(in_1), .b(in_2), .out(adder_1_out), .cin(1'b0), .cout(adder_1_cout[4]));
  \_4位并行加法器  \u_4位并行加法器_1  (
    .CI(1'b0), .A0(in_1[0]), .B0(in_2[0]), .A1(in_1[1]), .B1(in_2[1]), .A2(in_1[2]), .B2(in_2[2]),
    .A3(in_1[3]), .B3(in_2[3]), .S0(\n4位并行加法器_1_s0 [0]), .S1(\n4位并行加法器_1_s0 [1]), .S2(\n4位并行加法器_1_s0 [2]),
    .S3(\n4位并行加法器_1_s0 [3]), .CO(\n4位并行加法器_1_co [4]));
  Comparator #(.width(5)) comparator_1 (
    .a({\n4位并行加法器_1_co [4], \n4位并行加法器_1_s0 }), .b({adder_1_cout[4], adder_1_out}), .eq(out_3));  // open: gt, lt
endmodule

module \_16位并行加法器_FA单元  (
  input  CI,
  input  A,
  input  B,
  output P,
  output G,
  output S,
  output CO
);

  wire CIP_out;

  xor u_P (P, A, B);
  and u_G (G, A, B);
  and CIP (CIP_out, P, CI);
  or or_1 (CO, G, CIP_out);
  xor xor_1 (S, CI, P);
endmodule

module \_16位并行加法器_4位并行进位单元  (
  input  CI,
  input  P0,
  input  G0,
  input  P1,
  input  G1,
  input  P2,
  input  G2,
  input  P3,
  input  G3,
  output P_star,
  output CO0,
  output CO1,
  output CO2,
  output CO3,
  output G_star
);

  wire CIP0_out, CIP0P1_out, CIP0P1P2_out, CIP0P1P2P3_out, G0P1_out, G0P1P2_out, G0P1P2P3_out, G1P2_out,
       G1P2P3_out, G2P3_out, P0P1_out, P0P1P2_out, P1P2_out, P1P2P3_out, P2P3_out;

  and CIP0 (CIP0_out, CI, P0);
  and G0P1 (G0P1_out, G0, P1);
  and G1P2 (G1P2_out, G1, P2);
  and G2P3 (G2P3_out, G2, P3);
  and P0P1 (P0P1_out, P0, P1);
  and P1P2 (P1P2_out, P1, P2);
  and P2P3 (P2P3_out, P2, P3);
  and CIP0P1 (CIP0P1_out, CI, P0P1_out);
  and G0P1P2 (G0P1P2_out, G0, P1P2_out);
  and G1P2P3 (G1P2P3_out, G1, P2P3_out);
  and P0P1P2 (P0P1P2_out, P0, P1P2_out);
  and P1P2P3 (P1P2P3_out, P1, P2P3_out);
  and CIP0P1P2 (CIP0P1P2_out, CI, P0P1P2_out);
  and G0P1P2P3 (G0P1P2P3_out, G0, P1P2P3_out);
  and P0P1P2P3 (P_star, P0, P1P2P3_out);
  and CIP0P1P2P3 (CIP0P1P2P3_out, CI, P_star);
  or u_CO0 (CO0, G0, CIP0_out);
  or u_CO1 (CO1, G1, G0P1_out, CIP0P1_out);
  or u_CO2 (CO2, G2, G1P2_out, G0P1P2_out, CIP0P1P2_out);
  or u_CO3 (CO3, G3, G2P3_out, G1P2P3_out, G0P1P2P3_out, CIP0P1P2P3_out);
  or or_1 (G_star, G3, G2P3_out, G1P2P3_out, G0P1P2P3_out);
endmodule

module \_16位并行加法器_4位加法器单元  (
  input  CI,
  input  A0,
  input  B0,
  input  A1,
  input  B1,
  input  A2,
  input  B2,
  input  A3,
  input  B3,
  output S0,
  output CO,
  output S1,
  output S2,
  output S3,
  output P,
  output G
);

  wire \n16位并行加法器_4位并行进位单元_1_co0 , \n16位并行加法器_4位并行进位单元_1_co1 , \n16位并行加法器_4位并行进位单元_1_co2 ,
       \n16位并行加法器_fa单元_1_g , \n16位并行加法器_fa单元_1_p , \n16位并行加法器_fa单元_2_g , \n16位并行加法器_fa单元_2_p ,
       \n16位并行加法器_fa单元_3_g , \n16位并行加法器_fa单元_3_p , \n16位并行加法器_fa单元_4_g , \n16位并行加法器_fa单元_4_p ;

  \_16位并行加法器_FA单元  \u_16位并行加法器_fa单元_1  (
    .A(A0), .B(B0), .P(\n16位并行加法器_fa单元_1_p ), .G(\n16位并行加法器_fa单元_1_g ), .CI(CI), .S(S0));  // open: CO
  \_16位并行加法器_FA单元  \u_16位并行加法器_fa单元_2  (
    .A(A1), .B(B1), .P(\n16位并行加法器_fa单元_2_p ), .G(\n16位并行加法器_fa单元_2_g ), .CI(\n16位并行加法器_4位并行进位单元_1_co0 ),
    .S(S1));  // open: CO
  \_16位并行加法器_FA单元  \u_16位并行加法器_fa单元_3  (
    .A(A2), .B(B2), .P(\n16位并行加法器_fa单元_3_p ), .G(\n16位并行加法器_fa单元_3_g ), .CI(\n16位并行加法器_4位并行进位单元_1_co1 ),
    .S(S2));  // open: CO
  \_16位并行加法器_FA单元  \u_16位并行加法器_fa单元_4  (
    .A(A3), .B(B3), .P(\n16位并行加法器_fa单元_4_p ), .G(\n16位并行加法器_fa单元_4_g ), .CI(\n16位并行加法器_4位并行进位单元_1_co2 ),
    .S(S3));  // open: CO
  \_16位并行加法器_4位并行进位单元  \u_16位并行加法器_4位并行进位单元_1  (
    .CI(CI), .P0(\n16位并行加法器_fa单元_1_p ), .G0(\n16位并行加法器_fa单元_1_g ), .P1(\n16位并行加法器_fa单元_2_p ),
    .G1(\n16位并行加法器_fa单元_2_g ), .P2(\n16位并行加法器_fa单元_3_p ), .G2(\n16位并行加法器_fa单元_3_g ),
    .P3(\n16位并行加法器_fa单元_4_p ), .G3(\n16位并行加法器_fa单元_4_g ), .P_star(P), .CO0(\n16位并行加法器_4位并行进位单元_1_co0 ),
    .CO1(\n16位并行加法器_4位并行进位单元_1_co1 ), .CO2(\n16位并行加法器_4位并行进位单元_1_co2 ), .CO3(CO), .G_star(G));
endmodule

module \_16位并行加法器  (
  input  CI,
  input  [15:0] A,
  input  [15:0] B,
  output CO,
  output P,
  output G,
  output [15:0] S
);

  wire \n16位并行加法器_4位加法器单元_1_g , \n16位并行加法器_4位加法器单元_1_p , \n16位并行加法器_4位加法器单元_2_g , \n16位并行加法器_4位加法器单元_2_p ,
       \n16位并行加法器_4位加法器单元_3_g , \n16位并行加法器_4位加法器单元_3_p , \n16位并行加法器_4位加法器单元_4_g , \n16位并行加法器_4位加法器单元_4_p ,
       \n16位并行加法器_4位并行进位单元_1_co0 , \n16位并行加法器_4位并行进位单元_1_co1 , \n16位并行加法器_4位并行进位单元_1_co2 ;

  \_16位并行加法器_4位加法器单元  \u_16位并行加法器_4位加法器单元_1  (
    .CI(CI), .A0(A[0]), .B0(B[0]), .A1(A[1]), .B1(B[1]), .A2(A[2]), .B2(B[2]), .A3(A[3]), .B3(B[3]),
    .S3(S[3]), .S2(S[2]), .S1(S[1]), .S0(S[0]), .P(\n16位并行加法器_4位加法器单元_1_p ), .G(\n16位并行加法器_4位加法器单元_1_g ));  // open: CO
  \_16位并行加法器_4位加法器单元  \u_16位并行加法器_4位加法器单元_2  (
    .CI(\n16位并行加法器_4位并行进位单元_1_co0 ), .A0(A[4]), .B0(B[4]), .A1(A[5]), .B1(B[5]), .A2(A[6]), .B2(B[6]),
    .A3(A[7]), .B3(B[7]), .S3(S[7]), .S2(S[6]), .S1(S[5]), .S0(S[4]), .P(\n16位并行加法器_4位加法器单元_2_p ),
    .G(\n16位并行加法器_4位加法器单元_2_g ));  // open: CO
  \_16位并行加法器_4位加法器单元  \u_16位并行加法器_4位加法器单元_3  (
    .CI(\n16位并行加法器_4位并行进位单元_1_co1 ), .A0(A[8]), .B0(B[8]), .A1(A[9]), .B1(B[9]), .A2(A[10]), .B2(B[10]),
    .A3(A[11]), .B3(B[11]), .S3(S[11]), .S2(S[10]), .S1(S[9]), .S0(S[8]), .P(\n16位并行加法器_4位加法器单元_3_p ),
    .G(\n16位并行加法器_4位加法器单元_3_g ));  // open: CO
  \_16位并行加法器_4位加法器单元  \u_16位并行加法器_4位加法器单元_4  (
    .CI(\n16位并行加法器_4位并行进位单元_1_co2 ), .A0(A[12]), .B0(B[12]), .A1(A[13]), .B1(B[13]), .A2(A[14]), .B2(B[14]),
    .A3(A[15]), .B3(B[15]), .S3(S[15]), .S2(S[14]), .S1(S[13]), .S0(S[12]), .P(\n16位并行加法器_4位加法器单元_4_p ),
    .G(\n16位并行加法器_4位加法器单元_4_g ));  // open: CO
  \_16位并行加法器_4位并行进位单元  \u_16位并行加法器_4位并行进位单元_1  (
    .CI(CI), .P0(\n16位并行加法器_4位加法器单元_1_p ), .G0(\n16位并行加法器_4位加法器单元_1_g ), .P1(\n16位并行加法器_4位加法器单元_2_p ),
    .G1(\n16位并行加法器_4位加法器单元_2_g ), .P2(\n16位并行加法器_4位加法器单元_3_p ), .G2(\n16位并行加法器_4位加法器单元_3_g ),
    .P3(\n16位并行加法器_4位加法器单元_4_p ), .G3(\n16位并行加法器_4位加法器单元_4_g ), .P_star(P), .CO0(\n16位并行加法器_4位并行进位单元_1_co0 ),
    .CO1(\n16位并行加法器_4位并行进位单元_1_co1 ), .CO2(\n16位并行加法器_4位并行进位单元_1_co2 ), .CO3(CO), .G_star(G));
endmodule

module \test_16位并行加法器  (
  input  in_1,
  input  in_2,
  input  in_3,
  input  in_4,
  input  in_5,
  output [15:0] out_6,
  output [16:0] out_7,
  output [15:0] out_8,
  output [16:0] out_9
);

  wire and_1_out, clock_1_out, comparator_1_eq;

  Clock clock_1 (.out(clock_1_out));
  and and_1 (and_1_out, in_1, comparator_1_eq);
  Random #(.width(16)) random_1 (.clk(clock_1_out), .next(and_1_out), .out(out_6), .clr(in_3));
  Random #(.width(16), .seed(12)) random_2 (.clk(clock_1_out), .next(and_1_out), .out(out_8), .clr(in_4));
  \_16位并行加法器  \u_16位并行加法器_1  (.A(out_6), .B(out_8), .CO(out_7[16]), .S(out_7[15:0]), .CI(in_2));  // open: P, G
  Adder #(.width(16)) adder_1 (.a(out_6), .b(out_8), .out(out_9[15:0]), .cin(in_5), .cout(out_9[16]));
  Comparator #(.width(17)) comparator_1 (.a(out_7), .b(out_9), .eq(comparator_1_eq));  // open: gt, lt
endmodule

module \RS触发器  (
  input  Rd,
  input  Sd,
  output Q,
  output Q_prime
);

  nor nor_1 (Q, Rd, Q_prime);
  nor nor_2 (Q_prime, Q, Sd);
endmodule

module \D触发器  (
  input  L,
  input  D,
  output Q,
  output Q_prime
);

  wire and_1_out, and_2_out, not_1_out;

  not not_1 (not_1_out, D);
  and and_1 (and_1_out, not_1_out, L);
  and and_2 (and_2_out, L, D);
  nor nor_1 (Q, and_1_out, Q_prime);
  nor nor_2 (Q_prime, Q, and_2_out);
endmodule

module \边沿触发器  (
  input  L,
  input  D,
  input  en,
  output Q
);

  wire and_1_out, \d触发器_1_q , not_1_out;

  and and_1 (and_1_out, D, en);
  not not_1 (not_1_out, L);
  \D触发器  \d触发器_1  (.L(not_1_out), .D(and_1_out), .Q(\d触发器_1_q ));  // open: Q_prime
  \D触发器  \d触发器_2  (.L(L), .D(\d触发器_1_q ), .Q(Q));  // open: Q_prime
endmodule

module \反馈电路_分频  (
  input  in_1
);

  wire d_ff_1_qn, d_ff_2_q, d_ff_2_qn, d_ff_3_qn;
  wire [0:0] clock_1_out, d_ff_1_q, d_ff_3_q;
  wire [4:4] not_1_out;

  Clock clock_1 (.out(clock_1_out[0]));
  not not_1 (not_1_out[4], 1'b0);
  D_Flip_Flop d_ff_1 (.clk(clock_1_out[0]), .D(d_ff_1_qn), .Q(d_ff_1_q[0]), .Qn(d_ff_1_qn));  // open: preset, en, reset
  D_Flip_Flop d_ff_2 (.clk(clock_1_out[0]), .D(d_ff_2_qn), .Q(d_ff_2_q), .Qn(d_ff_2_qn));  // open: preset, en, reset
  D_Flip_Flop d_ff_3 (.clk(d_ff_2_q), .D(d_ff_3_qn), .Q(d_ff_3_q[0]), .Qn(d_ff_3_qn));  // open: preset, en, reset
  TTY tty_1 (.data({1'b0, {2{not_1_out[4]}}, 3'b000, clock_1_out[0]}), .clk(clock_1_out[0]), .clr(in_1));  // open: we
  TTY tty_2 (.data({1'b0, {2{not_1_out[4]}}, 3'b000, d_ff_1_q[0]}), .clk(clock_1_out[0]), .clr(in_1));  // open: we
  TTY tty_3 (.data({1'b0, {2{not_1_out[4]}}, 3'b000, d_ff_3_q[0]}), .clk(clock_1_out[0]), .clr(in_1));  // open: we
endmodule

module \应用1_计算器  (
  input  clear,
  output [15:0] out_2,
  output out_3
);

  wire _0_out, _1_out, _2_out, _3_out, _4_out, _5_out, _6_out, _7_out, _8_out, _9_out, button_out,
       clock_1_out;
  wire [3:0] \应用1_按键转换_1__0_2 , \应用1_按键转换_1__1_2 , \应用1_按键转换_1__2_2 , \应用1_按键转换_1__3_2 ;
  wire [15:0] demultiplexer_1_out0, demultiplexer_1_out1, register_1_q, register_2_q, \应用1_按键转换_1_out ;

  Clock clock_1 (.out(clock_1_out));
  Button _1 (.out(_1_out));
  Button _2 (.out(_2_out));
  Button _3 (.out(_3_out));
  Button _4 (.out(_4_out));
  Button _5 (.out(_5_out));
  Button _6 (.out(_6_out));
  Button _7 (.out(_7_out));
  Button _8 (.out(_8_out));
  Button _9 (.out(_9_out));
  Button _0 (.out(_0_out));
  Button button (.out(button_out));
  Hex_Digit_Display hex_digit_display_1 (.value(\应用1_按键转换_1__3_2 ));  // open: dp
  Hex_Digit_Display hex_digit_display_2 (.value(\应用1_按键转换_1__2_2 ));  // open: dp
  \应用1_按键转换  \u_应用1_按键转换_1  (
    .CLK(clock_1_out), .clear(clear), ._1(_1_out), ._2(_2_out), ._3(_3_out), ._4(_4_out), ._5(_5_out),
    ._6(_6_out), ._7(_7_out), ._8(_8_out), ._9(_9_out), ._0(_0_out), .OUT(\应用1_按键转换_1_out ),
    ._3_2(\应用1_按键转换_1__3_2 ), ._2_2(\应用1_按键转换_1__2_2 ), ._1_2(\应用1_按键转换_1__1_2 ), ._0_2(\应用1_按键转换_1__0_2 ));
  Hex_Digit_Display hex_digit_display_3 (.value(\应用1_按键转换_1__0_2 ));  // open: dp
  Hex_Digit_Display hex_digit_display_4 (.value(\应用1_按键转换_1__1_2 ));  // open: dp
  Demultiplexer #(.width(16)) demultiplexer_1 (
    .out0(demultiplexer_1_out0), .out1(demultiplexer_1_out1), .in(\应用1_按键转换_1_out ));  // open: sel, en
  Register #(.width(16)) register_1 (.D(demultiplexer_1_out0), .Q(register_1_q));  // open: en, clk, clr
  Register #(.width(16)) register_2 (.D(demultiplexer_1_out1), .Q(register_2_q));  // open: en, clk, clr
  Adder #(.width(16)) adder_1 (.a(register_1_q), .b(register_2_q), .out(out_2), .cout(out_3));  // open: cin
endmodule

module \应用1_按键转换  (
  input  CLK,
  input  clear,
  input  _1,
  input  _2,
  input  _3,
  input  _4,
  input  _5,
  input  _6,
  input  _7,
  input  _8,
  input  _9,
  input  _0,
  output [3:0] _2_2,
  output [3:0] _0_2,
  output [3:0] _3_2,
  output [3:0] _1_2,
  output [15:0] OUT
);

  wire and_1_out, or_1_out, or_2_out, or_3_out, or_4_out, or_5_out, \应用1_译码器_1_1_a , \应用1_译码器_1_1_b ,
       \应用1_译码器_1_1_c , \应用1_译码器_1_1_d , \应用1_译码器_3_1_e0 , \应用1_译码器_3_1_e1 , \应用1_译码器_3_1_e2 ,
       \应用1_译码器_3_1_e3 , \按键高脉冲_out ;
  wire [2:0] counter_1_q;
  wire [3:0] and_2_out, and_6_out, and_10_out, and_14_out, register_1_q, register_2_q, register_3_q,
       register_4_q, register_5_q, \应用1_译码器_2_1_h ;
  wire [7:0] adder_1_out, bit_extender_1_out, bit_extender_2_out, multiplier_1_out, \应用1_译码器_3_1_c0 ;
  wire [15:0] adder_2_out, bit_extender_3_out, bit_extender_4_out, bit_extender_5_out, multiplier_2_out,
       multiplier_3_out;

  or or_1 (or_1_out, _1, _3, _5, _7, _9);
  or or_2 (or_2_out, _2, _3, _6, _7);
  or or_3 (or_3_out, _4, _5, _6, _7);
  or or_4 (or_4_out, _8, _9);
  or \u_按键高脉冲  (\按键高脉冲_out , _0, _9, _8, _7, _6, _5, _4, _3, _2, _1);
  or or_5 (or_5_out, clear, and_1_out);
  and and_1 (and_1_out, counter_1_q[2], counter_1_q[0]);
  Counter #(.width(3), .max('h7)) counter_1 (
    .Q(counter_1_q), .clk(\按键高脉冲_out ), .clr(or_5_out));  // open: load, D, count, carry
  and and_2 (and_2_out[0], \应用1_译码器_1_1_d , or_1_out);
  and and_3 (and_2_out[1], \应用1_译码器_1_1_d , or_2_out);
  and and_4 (and_2_out[2], \应用1_译码器_1_1_d , or_3_out);
  and and_5 (and_2_out[3], \应用1_译码器_1_1_d , or_4_out);
  and and_6 (and_6_out[0], \应用1_译码器_1_1_c , or_1_out);
  and and_7 (and_6_out[1], \应用1_译码器_1_1_c , or_2_out);
  and and_8 (and_6_out[2], \应用1_译码器_1_1_c , or_3_out);
  and and_9 (and_6_out[3], \应用1_译码器_1_1_c , or_4_out);
  and and_10 (and_10_out[0], \应用1_译码器_1_1_b , or_1_out);
  and and_11 (and_10_out[1], \应用1_译码器_1_1_b , or_2_out);
  and and_12 (and_10_out[2], \应用1_译码器_1_1_b , or_3_out);
  and and_13 (and_10_out[3], \应用1_译码器_1_1_b , or_4_out);
  and and_14 (and_14_out[0], \应用1_译码器_1_1_a , or_1_out);
  and and_15 (and_14_out[1], \应用1_译码器_1_1_a , or_2_out);
  and and_16 (and_14_out[2], \应用1_译码器_1_1_a , or_3_out);
  and and_17 (and_14_out[3], \应用1_译码器_1_1_a , or_4_out);
  \应用1_译码器_1  \u_应用1_译码器_1_1  (
    .Q0(counter_1_q[2]), .Q1(counter_1_q[1]), .Q2(counter_1_q[0]), .A(\应用1_译码器_1_1_a ), .B(\应用1_译码器_1_1_b ),
    .C(\应用1_译码器_1_1_c ), .D(\应用1_译码器_1_1_d ));
  \应用1_译码器_2  \u_应用1_译码器_2_1  (
    .R(clear), .A(\应用1_译码器_1_1_a ), .B(\应用1_译码器_1_1_b ), .C(\应用1_译码器_1_1_c ), .D(\应用1_译码器_1_1_d ),
    .E(\应用1_译码器_2_1_h [3]), .F(\应用1_译码器_2_1_h [2]), .G(\应用1_译码器_2_1_h [1]), .H(\应用1_译码器_2_1_h [0]));
  Register #(.width(4)) register_1 (.D(\应用1_译码器_2_1_h ), .Q(register_1_q), .clk(CLK));  // open: en, clr
  Register #(.width(4), .trigger("high")) register_2 (
    .D(and_2_out), .Q(register_2_q), .clk(register_1_q[0]));  // open: en, clr
  Register #(.width(4), .trigger("high")) register_3 (
    .D(and_6_out), .Q(register_3_q), .clk(register_1_q[1]));  // open: en, clr
  Register #(.width(4), .trigger("high")) register_4 (
    .D(and_10_out), .Q(register_4_q), .clk(register_1_q[2]));  // open: en, clr
  Register #(.width(4), .trigger("high")) register_5 (
    .D(and_14_out), .Q(register_5_q), .clk(register_1_q[3]));  // open: en, clr
  \应用1_译码器_3  \u_应用1_译码器_3_1  (
    .E(register_1_q[3]), .F(register_1_q[2]), .G(register_1_q[1]), .H(register_1_q[0]),
    .E0(\应用1_译码器_3_1_e0 ), .E1(\应用1_译码器_3_1_e1 ), .E2(\应用1_译码器_3_1_e2 ), .E3(\应用1_译码器_3_1_e3 ),
    .C1(\应用1_译码器_3_1_c0 [1]), .C0(\应用1_译码器_3_1_c0 [0]), .C3(\应用1_译码器_3_1_c0 [3]), .C2(\应用1_译码器_3_1_c0 [2]),
    .C5(\应用1_译码器_3_1_c0 [5]), .C4(\应用1_译码器_3_1_c0 [4]), .C6(\应用1_译码器_3_1_c0 [6]), .C7(\应用1_译码器_3_1_c0 [7]));
  // Probe on register_2_q
  // Probe on register_3_q
  // Probe on register_4_q
  // Probe on register_5_q
  Hex_Digit_Display hex_digit_display_1 (.value(_3_2));  // open: dp
  \应用1_Crossbar  \u_应用1_crossbar_1  (
    .D0(register_2_q), .D1(register_3_q), .D2(register_4_q), .D3(register_5_q), .OUT0(_0_2), .OUT1(_1_2),
    .OUT2(_2_2), .OUT3(_3_2), .\控制信号 (\应用1_译码器_3_1_c0 ), .E2(\应用1_译码器_3_1_e2 ), .E3(\应用1_译码器_3_1_e3 ),
    .E1(\应用1_译码器_3_1_e1 ), .E0(\应用1_译码器_3_1_e0 ));
  Hex_Digit_Display hex_digit_display_2 (.value(_2_2));  // open: dp
  Hex_Digit_Display hex_digit_display_3 (.value(_1_2));  // open: dp
  Hex_Digit_Display hex_digit_display_4 (.value(_0_2));  // open: dp
  assign bit_extender_1_out = {{4{1'b0}}, _0_2};  // Bit_Extender bit_extender_1
  assign bit_extender_2_out = {{4{1'b0}}, _1_2};  // Bit_Extender bit_extender_2
  assign bit_extender_3_out = {{12{1'b0}}, _2_2};  // Bit_Extender bit_extender_3
  assign bit_extender_4_out = {{12{1'b0}}, _3_2};  // Bit_Extender bit_extender_4
  Multiplier multiplier_1 (.a(bit_extender_2_out), .b(8'ha), .out(multiplier_1_out));  // open: cin, cout
  Multiplier #(.width(16)) multiplier_2 (
    .a(bit_extender_3_out), .b(16'h64), .out(multiplier_2_out));  // open: cin, cout
  Multiplier #(.width(16)) multiplier_3 (
    .a(bit_extender_4_out), .b(16'h3e8), .out(multiplier_3_out));  // open: cin, cout
  Adder adder_1 (.a(bit_extender_1_out), .b(multiplier_1_out), .out(adder_1_out));  // open: cin, cout
  Adder #(.width(16)) adder_2 (.a(multiplier_2_out), .b(multiplier_3_out), .out(adder_2_out));  // open: cin, cout
  assign bit_extender_5_out = {{8{1'b0}}, adder_1_out};  // Bit_Extender bit_extender_5
  Adder #(.width(16)) adder_3 (.a(bit_extender_5_out), .b(adder_2_out), .out(OUT));  // open: cin, cout

  // Notes on the sheet:
  //   解决组合逻辑竞争冒险
endmodule

module \应用1_译码器_1  (
  input  Q0,
  input  Q1,
  input  Q2,
  output A,
  output B,
  output C,
  output D
);

  wire not_1_out, not_2_out, not_3_out, not_4_out, not_5_out, not_6_out, not_7_out;

  not not_1 (not_1_out, Q1);
  not not_2 (not_2_out, Q2);
  not not_3 (not_3_out, Q0);
  not not_4 (not_4_out, Q0);
  not not_5 (not_5_out, Q2);
  not not_6 (not_6_out, Q0);
  not not_7 (not_7_out, Q1);
  and and_1 (A, Q0, not_1_out, not_2_out);
  and and_2 (B, not_3_out, Q1, Q2);
  and and_3 (C, not_4_out, Q1, not_5_out);
  and and_4 (D, not_6_out, not_7_out, Q2);
endmodule

module \应用1_译码器_2  (
  input  R,
  input  A,
  input  B,
  input  C,
  input  D,
  output E,
  output F,
  output G,
  output H
);

  wire and_1_out, and_2_out, and_3_out, and_4_out, and_5_out, and_6_out, and_7_out, and_8_out, and_9_out,
       and_10_out, not_1_out, not_2_out, not_3_out, not_4_out, not_5_out, not_6_out, not_7_out, not_8_out,
       not_9_out, not_10_out, not_11_out, not_12_out, not_13_out, not_14_out, not_15_out, not_16_out,
       not_17_out, not_18_out, not_19_out, not_20_out, not_21_out, not_22_out, not_23_out, not_24_out,
       not_25_out, not_26_out, not_27_out, not_28_out, not_29_out, not_30_out, not_31_out, not_32_out,
       not_33_out, not_34_out;

  not not_1 (not_1_out, A);
  not not_2 (not_2_out, B);
  not not_3 (not_3_out, C);
  not not_4 (not_4_out, D);
  not not_5 (not_5_out, A);
  not not_6 (not_6_out, B);
  not not_7 (not_7_out, C);
  not not_8 (not_8_out, A);
  not not_9 (not_9_out, B);
  not not_10 (not_10_out, D);
  not not_11 (not_11_out, A);
  not not_12 (not_12_out, C);
  not not_13 (not_13_out, D);
  not not_14 (not_14_out, A);
  not not_15 (not_15_out, B);
  not not_16 (not_16_out, C);
  not not_17 (not_17_out, D);
  not not_18 (not_18_out, A);
  not not_19 (not_19_out, B);
  not not_20 (not_20_out, C);
  not not_21 (not_21_out, A);
  not not_22 (not_22_out, B);
  not not_23 (not_23_out, D);
  not not_24 (not_24_out, A);
  not not_25 (not_25_out, B);
  not not_26 (not_26_out, C);
  not not_27 (not_27_out, D);
  not not_28 (not_28_out, A);
  not not_29 (not_29_out, B);
  not not_30 (not_30_out, C);
  not not_31 (not_31_out, A);
  not not_32 (not_32_out, B);
  not not_33 (not_33_out, C);
  not not_34 (not_34_out, D);
  and and_1 (and_1_out, not_1_out, not_2_out, not_3_out, not_4_out);
  and and_2 (and_2_out, not_5_out, not_6_out, not_7_out, D);
  and and_3 (and_3_out, not_8_out, not_9_out, C, not_10_out);
  and and_4 (and_4_out, not_11_out, B, not_12_out, not_13_out);
  and and_5 (and_5_out, not_14_out, not_15_out, not_16_out, not_17_out);
  and and_6 (and_6_out, not_18_out, not_19_out, not_20_out, D);
  and and_7 (and_7_out, not_21_out, not_22_out, C, not_23_out);
  and and_8 (and_8_out, not_24_out, not_25_out, not_26_out, not_27_out);
  and and_9 (and_9_out, not_28_out, not_29_out, not_30_out, D);
  and and_10 (and_10_out, not_31_out, not_32_out, not_33_out, not_34_out);
  or or_1 (E, R, and_1_out, and_2_out, and_3_out, and_4_out);
  or or_2 (F, R, and_5_out, and_6_out, and_7_out);
  or or_3 (G, R, and_8_out, and_9_out);
  or or_4 (H, R, and_10_out);
endmodule

module \应用1_译码器_3  (
  input  E,
  input  F,
  input  G,
  input  H,
  output E0,
  output E1,
  output E2,
  output E3,
  output C1,
  output C0,
  output C3,
  output C2,
  output C5,
  output C4,
  output C6,
  output C7
);

  wire and_1_out, and_2_out, and_3_out, and_4_out, and_5_out, and_6_out, and_7_out, and_8_out, and_9_out,
       and_11_out, and_12_out, and_13_out, and_14_out, not_1_out, not_2_out, not_3_out, not_4_out, not_5_out,
       not_6_out, not_7_out, not_8_out, not_9_out, not_10_out, not_11_out, not_12_out, not_13_out,
       not_14_out, not_15_out, not_16_out, not_17_out, not_18_out, not_19_out, not_20_out, not_21_out,
       not_22_out, not_23_out, not_24_out, not_25_out, not_26_out, not_27_out, not_28_out, not_29_out,
       not_30_out, not_31_out, not_32_out, not_33_out, not_34_out, not_35_out, not_36_out, not_37_out,
       not_38_out, not_39_out, not_40_out, not_41_out, not_42_out, not_43_out, not_44_out, not_45_out,
       not_46_out, not_47_out, not_48_out, not_49_out, not_50_out, not_51_out, not_52_out, not_53_out,
       not_54_out;

  not not_1 (not_1_out, H);
  not not_2 (not_2_out, G);
  not not_3 (not_3_out, H);
  not not_4 (not_4_out, F);
  not not_5 (not_5_out, G);
  not not_6 (not_6_out, H);
  not not_7 (not_7_out, E);
  not not_8 (not_8_out, F);
  not not_9 (not_9_out, G);
  not not_10 (not_10_out, H);
  not not_11 (not_11_out, G);
  not not_12 (not_12_out, H);
  not not_13 (not_13_out, F);
  not not_14 (not_14_out, G);
  not not_15 (not_15_out, H);
  not not_16 (not_16_out, E);
  not not_17 (not_17_out, F);
  not not_18 (not_18_out, G);
  not not_19 (not_19_out, H);
  not not_20 (not_20_out, F);
  not not_21 (not_21_out, G);
  not not_22 (not_22_out, H);
  not not_23 (not_23_out, E);
  not not_24 (not_24_out, F);
  not not_25 (not_25_out, G);
  not not_26 (not_26_out, H);
  not not_27 (not_27_out, E);
  not not_28 (not_28_out, F);
  not not_29 (not_29_out, G);
  not not_30 (not_30_out, H);
  not not_31 (not_31_out, F);
  not not_32 (not_32_out, G);
  not not_33 (not_33_out, H);
  not not_34 (not_34_out, E);
  not not_35 (not_35_out, F);
  not not_36 (not_36_out, G);
  not not_37 (not_37_out, H);
  not not_38 (not_38_out, G);
  not not_39 (not_39_out, H);
  not not_40 (not_40_out, E);
  not not_41 (not_41_out, F);
  not not_42 (not_42_out, G);
  not not_43 (not_43_out, H);
  not not_44 (not_44_out, E);
  not not_45 (not_45_out, F);
  not not_46 (not_46_out, G);
  not not_47 (not_47_out, H);
  not not_48 (not_48_out, F);
  not not_49 (not_49_out, G);
  not not_50 (not_50_out, H);
  not not_51 (not_51_out, E);
  not not_52 (not_52_out, F);
  not not_53 (not_53_out, G);
  not not_54 (not_54_out, H);
  and and_1 (and_1_out, E, F, G, not_1_out);
  and and_2 (and_2_out, E, F, not_2_out, not_3_out);
  and and_3 (and_3_out, E, not_4_out, not_5_out, not_6_out);
  and and_4 (and_4_out, not_7_out, not_8_out, not_9_out, not_10_out);
  and and_5 (and_5_out, E, F, not_11_out, not_12_out);
  or or_1 (E1, and_5_out, and_6_out, and_7_out);
  and and_6 (and_6_out, E, not_13_out, not_14_out, not_15_out);
  and and_7 (and_7_out, not_16_out, not_17_out, not_18_out, not_19_out);
  and and_8 (and_8_out, E, not_20_out, not_21_out, not_22_out);
  or or_2 (E2, and_8_out, and_9_out);
  and and_9 (and_9_out, not_23_out, not_24_out, not_25_out, not_26_out);
  and and_10 (E3, not_27_out, not_28_out, not_29_out, not_30_out);
  and and_11 (and_11_out, E, not_31_out, not_32_out, not_33_out);
  or or_3 (C1, and_11_out, and_12_out);
  and and_12 (and_12_out, not_34_out, not_35_out, not_36_out, not_37_out);
  and and_13 (and_13_out, E, F, not_38_out, not_39_out);
  or or_4 (C0, and_13_out, and_14_out);
  and and_14 (and_14_out, not_40_out, not_41_out, not_42_out, not_43_out);
  and and_15 (C3, not_44_out, not_45_out, not_46_out, not_47_out);
  and and_16 (C2, E, not_48_out, not_49_out, not_50_out);
  and and_17 (C4, not_51_out, not_52_out, not_53_out, not_54_out);
  or or_5 (E0, and_1_out, and_2_out, and_3_out, and_4_out);

  assign C5 = 1'b0;
  assign C6 = 1'b0;
  assign C7 = 1'b0;
endmodule

module \应用1_Crossbar  (
  input  E0,
  input  E1,
  input  E2,
  input  E3,
  input  [3:0] D0,
  input  [3:0] D1,
  input  [3:0] D2,
  input  [3:0] D3,
  input  [7:0] \控制信号 ,
  output [3:0] OUT2,
  output [3:0] OUT0,
  output [3:0] OUT1,
  output [3:0] OUT3
);

  Pull_Resistor pull_resistor_1 (.node(OUT0));
  Multiplexer #(.select(2), .width(4)) multiplexer_1 (
    .in0(D0), .in1(D1), .in2(D2), .in3(D3), .out(OUT0), .sel(\控制信号 [1:0]), .en(E0));
  Pull_Resistor pull_resistor_2 (.node(OUT1));
  Multiplexer #(.select(2), .width(4)) multiplexer_2 (
    .in0(D0), .in1(D1), .in2(D2), .in3(D3), .out(OUT1), .sel(\控制信号 [3:2]), .en(E1));
  Pull_Resistor pull_resistor_3 (.node(OUT2));
  Multiplexer #(.select(2), .width(4)) multiplexer_3 (
    .in0(D0), .in1(D1), .in2(D2), .in3(D3), .out(OUT2), .sel(\控制信号 [5:4]), .en(E2));
  Pull_Resistor pull_resistor_4 (.node(OUT3));
  Multiplexer #(.select(2), .width(4)) multiplexer_4 (
    .in0(D0), .in1(D1), .in2(D2), .in3(D3), .out(OUT3), .sel(\控制信号 [7:6]), .en(E3));
endmodule

module \竞争冒险  (
  input  in_1,
  output [7:0] out_2
);

  wire and_1_out, clock_1_out, d_ff_1_q, not_1_out;

  Clock clock_1 (.out(clock_1_out));
  not not_1 (not_1_out, in_1);
  and and_1 (and_1_out, not_1_out, in_1);
  D_Flip_Flop d_ff_1 (.clk(clock_1_out), .D(and_1_out), .Q(d_ff_1_q));  // open: Qn, preset, en, reset
  Counter counter_1 (.Q(out_2), .clk(d_ff_1_q));  // open: load, D, count, carry, clr
endmodule
